// Logisim project FULL ADDER.circ as structural Verilog: 1 circuit, main circuit main
module main (
  input  in_1,
  input  in_2,
  input  in_3,
  output out_4,
  output out_5
);

  wire and_1_out, and_2_out, xor_1_out;

  and and_1 (and_1_out, in_2, in_1);
  xor xor_1 (xor_1_out, in_1, in_2);
  and and_2 (and_2_out, xor_1_out, in_3);
  or or_1 (out_5, and_2_out, and_1_out);
  xor xor_2 (out_4, xor_1_out, in_3);
endmodule
